# Fritzing sketch Schematics (saved by Fritzing 0.9.5d)
breadboards: 1

parts:
  Компонент1 = Arduino Uno (Rev3) - ICSP
  ACC_PIN_17_(BUS+) = female pin header, 1 pin [form="♀ (female)"]
  PIN_7_(GND) = female pin header, 1 pin [form="♀ (female)"]
  D1 = Schottky Diode [part_number=1N5817 package="300 mil [THT]"]
  FRONT_PANEL_CHIP_15_(ROW) = female pin header, 1 pin [form="♀ (female)"]
  D2 = Schottky Diode [part_number=1N5817 package="300 mil [THT]"]
  R1 = Resistor [tolerance=±5% resistance=13k package=THT]
  D3 = Schottky Diode [part_number=1N5817 package="300 mil [THT]"]
  R2 = Resistor [tolerance=±5% resistance=22k package=THT]
  D4 = Schottky Diode [part_number=1N5817 package="300 mil [THT]"]
  R3 = Resistor [tolerance=±5% resistance=43k package=THT]
  FRONT_PANEL_CHIP_13_(COL) = female pin header, 1 pin [form="♀ (female)"]
  R4 = Resistor [tolerance=±5% resistance=13k package=THT]
  R5 = Resistor [tolerance=±5% resistance=22k package=THT]
  R6 = Resistor [tolerance=±5% resistance=43k package=THT]
  D5 = Schottky Diode [part_number=1N5817 package="300 mil [THT]"]
  D6 = Schottky Diode [part_number=1N5817 package="300 mil [THT]"]
  D7 = Schottky Diode [part_number=1N5817 package="300 mil [THT]"]

nets:
  N1: Компонент1.ICSP_MOSI, Компонент1.D11_PWM/MOSI, D4.cathode
  N2: Компонент1.D8, D1.cathode
  N3: Компонент1.D9_PWM, D2.cathode
  N4: Компонент1.D10_PWM/SS, D3.cathode
  N5: Компонент1.D2, ACC_PIN_17_(BUS+).pin1
  N6: Компонент1.D5_PWM, D5.cathode
  N7: Компонент1.D6_PWM, D6.cathode
  N8: Компонент1.D7, D7.cathode
  N9: Компонент1.GND, PIN_7_(GND).pin1
  N10: D1.anode, FRONT_PANEL_CHIP_15_(ROW).pin1, R1.Pin_1
  N11: D2.anode, R1.Pin_0, R2.Pin_1
  N12: D3.anode, R2.Pin_0, R3.Pin_1
  N13: D4.anode, R3.Pin_0
  N14: FRONT_PANEL_CHIP_13_(COL).pin1, R4.Pin_1
  N15: R4.Pin_0, R5.Pin_1, D5.anode
  N16: R5.Pin_0, R6.Pin_1, D6.anode
  N17: R6.Pin_0, D7.anode
